# Fritzing sketch VSTVision32 (saved by Fritzing 1.0.6)

parts:
  Grove_Shield_for_XIAO_1 = Grove Shield for XIAO [package="DIP (Dual Inline) [THT]"]
  XIAO_ESP32S1 = XIAO ESP32S3 [package="DIP (Dual Inline) [THT]"]
  Grove_Vision_AI_Module_V1 = Grove Vision AI Module V2 [chip_label="Grove Vision AI Module V2\n" package="DIP (Dual Inline) [THT]"]  # not connected

nets:
  N1: Grove_Shield_for_XIAO_1.0, XIAO_ESP32S1.D0
  N2: Grove_Shield_for_XIAO_1.1, XIAO_ESP32S1.D1
  N3: Grove_Shield_for_XIAO_1.2, XIAO_ESP32S1.D2
  N4: Grove_Shield_for_XIAO_1.3, XIAO_ESP32S1.D3
  N5: Grove_Shield_for_XIAO_1.4, XIAO_ESP32S1.D4
  N6: Grove_Shield_for_XIAO_1.5, XIAO_ESP32S1.D5
  N7: Grove_Shield_for_XIAO_1.6, XIAO_ESP32S1.D6

custom parts:
  Grove Shield for XIAO: Seeed Studio Grove Base for XIAO is a plug-and-play Grove extension board for Seeed Studio XIAO. With the on-board battery management chip and battery bonding pad, you could easily power your Seeed Studio XIAO with lithium battery and recharge it. 8 Grove connectors onboard includes two Grove I2C and one UART. It acts as a bridge for Seeed Studio XIAO and Seeed's Grove system. Flash SPI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
  XIAO ESP32S3: Seeed Studio XIAO ESP32S3 leverages 240MHz Xtensa 32-bit LX7 dual-core processor, supporting both WiFi and BLE 5.0 wireless connectivities, a 2.4GHz Rod antenna, allows for deep sleep mode with power consumption as low as 14μA while supporting lithium battery charging management. Ideal for the Internet of Things, Smart Homes, Wireless wearable devices, Robotics, etc.
  Grove Vision AI Module V2: It is an MCU-based vision AI module powered by Arm Cortex-M55 & Ethos-U55. It supports TensorFlow and PyTorch frameworks and is compatible with Arduino IDE. With the SenseCraft AI algorithm platform, trained ML models can be deployed to the sensor without the need for coding. It features a standard CSI interface, an onboard digital microphone and an SD card slot, making it highly suitable for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
