# Fritzing sketch SIM7000-TB6612FNG-Shield (saved by Fritzing 1.0.6)
circuit board: 6cm x 3.55cm
breadboards: 1

parts:
  J3 = female pin header, 16 pins [form="♀ (female)"]
  J5 = female pin header, 7 pins [form="♀ (female)"]
  J6 = female pin header, 7 pins [form="♀ (female)"]
  J1 = female pin header, 16 pins [form="♀ (female)"]  # not connected
  J7 = male pin header, 4 pins [form="♂ (male)"]
  R3 = Resistor [tolerance=±5% resistance=470 power=0.25W package=THT]
  LED1 = LED - 3mm [color="Yellow (595nm)" current=0.030A package="3 mm [THT]"]
  LED3 = LED - 3mm [color="Yellow (595nm)" current=0.030A package="3 mm [THT]"]
  LED4 = LED - 3mm [color="Yellow (595nm)" current=0.030A package="3 mm [THT]"]
  R4 = Resistor [tolerance=±5% resistance=470 power=0.25W package=THT]
  R5 = Resistor [tolerance=±5% resistance=470 power=0.25W package=THT]
  R6 = Resistor [tolerance=±5% resistance=470 power=0.25W package=THT]
  C1 = Electrolytic Capacitor [capacitance=10µF voltage=35V package="100 mil [THT, electrolytic]"]
  J12 = female pin header, 8 pins [form="♀ (female)"]
  J11 = female pin header, 8 pins [form="♀ (female)"]
  LED2 = LED - 3mm [color="Yellow (595nm)" current=0.030A package="3 mm [THT]"]
  J8 = male pin header, 5 pins [form="♂ (male)"]
  J13 = male pin header, 2 pins [form="♂ (male)"]
  J14 = male pin header, 2 pins [form="♂ (male)"]
  J16 = male pin header, 3 pins [form="♂ (male)"]
  J17 = screw terminal, 2 pins
  R7 = Resistor [tolerance=±5% power=0.25W resistance=10k package=THT]

nets:
  N1: J3.pin1, J6.pin7
  N2: J3.pin2, J5.pin7
  N3: J3.pin3, J11.pin2, J16.pin2, R7.Pin_1
  N4: J3.pin4, C1.-, J11.pin3, J11.pin8, J17.pin1
  N5: J5.pin1, J12.pin1
  N6: J5.pin2, J12.pin2
  N7: J5.pin3, J12.pin3
  N8: J5.pin4, J12.pin5
  N9: J5.pin5, J7.pin2
  N10: J5.pin6, J7.pin1
  N11: J6.pin2, J7.pin4, J12.pin8
  N12: J6.pin3, J7.pin3
  N13: J6.pin4, J12.pin7
  N14: J6.pin5, J12.pin6
  N15: R3.Pin_0, R5.Pin_0, J11.pin1, J16.pin3, J17.pin2
  N16: R3.Pin_1, LED3.anode
  N17: LED1.cathode, J11.pin6, J8.pin4, J14.pin1
  N18: LED1.anode, R6.Pin_1
  N19: LED3.cathode, J11.pin4, J8.pin2, J13.pin1
  N20: LED4.cathode, J11.pin7, J8.pin5, J14.pin2
  N21: LED4.anode, R4.Pin_1
  N22: R5.Pin_1, LED2.anode
  N23: J12.pin4, R7.Pin_0
  N24: J11.pin5, LED2.cathode, J8.pin3, J13.pin2

notes:
  GND
  3V3
  SDA
  CLK
  RX
  TX
  D0
  D1
  T-SIM7000/7070G-S3
  XIAO-UART SM/DRV
  SM/DRV T-SIM7000/7070G bipolair
  D2
  D3
  TB6612FNG
  B2
  A2
  A1
  VCC
  B1
  STBY
  AIN1
  AIN2
  BIN2
  BIN1
  PWMA
  PWMB
  NC
  D10
  D9
  CH1
  CH2
  + EXT
  +  -
