# Fritzing sketch SIM7000-Vision-Shield-Relais (saved by Fritzing 1.0.6)
circuit board: 6cm x 3.55cm
breadboards: 1

parts:
  J3 = female pin header, 16 pins [form="♀ (female)"]
  J5 = female pin header, 7 pins [form="♀ (female)"]
  J6 = female pin header, 7 pins [form="♀ (female)"]
  J1 = female pin header, 16 pins [form="♀ (female)"]  # not connected
  R1 = Resistor [tolerance=±5% resistance=1k power=0.25W package=THT]
  R2 = Resistor [tolerance=±5% resistance=1k power=0.25W package=THT]
  Q1 = NPN-Transistor [part_number=BC337 package="TO92 [THT]"]
  Q2 = NPN-Transistor [part_number=BC337 package="TO92 [THT]"]
  J8 = screw terminal, 3 pins
  J7 = male pin header, 4 pins [form="♂ (male)"]
  LED1 = LED - 3mm [color="Red (633nm)" current=0.030A package="3 mm [THT]"]
  LED2 = LED - 3mm [color="Red (633nm)" current=0.030A package="3 mm [THT]"]
  D3 = Rectifier Diode [part_number=1N4001 package="300 mil [THT]"]
  D4 = Rectifier Diode [part_number=1N4001 package="300 mil [THT]"]
  J9 = screw terminal, 3 pins
  K2 = RELAY [package=relay-g5v]
  K1 = RELAY [package=relay-g5v]

nets:
  N1: J3.pin1, J6.pin7
  N2: J3.pin2, J5.pin7
  N3: J3.pin3, J6.pin3, J7.pin3, D3.cathode, D4.cathode, K2.2, K1.2
  N4: J3.pin4, J6.pin2, Q1.C, Q2.C, J7.pin4
  N5: J5.pin1, R1.Pin_1
  N6: J5.pin2, R2.Pin_1
  N7: J5.pin5, J7.pin2
  N8: J5.pin6, J7.pin1
  N9: R1.Pin_0, LED2.cathode
  N10: R2.Pin_0, LED1.cathode
  N11: Q1.E, D3.anode, K1.9
  N12: Q1.B, LED2.anode
  N13: Q2.E, D4.anode, K2.9
  N14: Q2.B, LED1.anode
  N15: J8.pin1, K1.1
  N16: J8.pin2, K1.6
  N17: J8.pin3, K1.10
  N18: J9.pin1, K2.1
  N19: J9.pin2, K2.6
  N20: J9.pin3, K2.10

notes:
  GND
  3V3
  SDA
  CLK
  RX
  TX
  GPIO1
  GPIO2
  NC
  NO
  C
  T-SIM7000/7070G
  XIAO - UART
  Rev. A
  UART - T-SIM7000G / T-SIM7070G
