# Fritzing sketch SIM7000-ULN2003-Shield (saved by Fritzing 1.0.6)
circuit board: 6cm x 3.55cm
breadboards: 1

parts:
  J3 = female pin header, 16 pins [form="♀ (female)"]
  J5 = female pin header, 7 pins [form="♀ (female)"]
  J6 = female pin header, 7 pins [form="♀ (female)"]
  J1 = female pin header, 16 pins [form="♀ (female)"]  # not connected
  J7 = male pin header, 4 pins [form="♂ (male)"]
  IC1 = IC, DIP package, 16 pins [chip_label=ULN2003]
  J8 = male pin header, 5 pins [form="♂ (male)"]
  R3 = Resistor [tolerance=±5% resistance=470 power=0.25W package=THT]
  LED1 = LED - 3mm [color="Yellow (595nm)" current=0.030A package="3 mm [THT]"]
  LED2 = LED - 3mm [color="Yellow (595nm)" current=0.030A package="3 mm [THT]"]
  LED3 = LED - 3mm [color="Yellow (595nm)" current=0.030A package="3 mm [THT]"]
  LED4 = LED - 3mm [color="Yellow (595nm)" current=0.030A package="3 mm [THT]"]
  R4 = Resistor [tolerance=±5% resistance=470 power=0.25W package=THT]
  R5 = Resistor [tolerance=±5% resistance=470 power=0.25W package=THT]
  R6 = Resistor [tolerance=±5% resistance=470 power=0.25W package=THT]
  C1 = Electrolytic Capacitor [capacitance=10µF voltage=35V package="100 mil [THT, electrolytic]"]
  R7 = Resistor [tolerance=±5% resistance=1k power=0.25W package=THT]  # not connected

nets:
  N1: J3.pin1, J6.pin7
  N2: J3.pin2, J5.pin7
  N3: J3.pin3, J6.pin3, J7.pin3, J8.pin1, R3.Pin_0, R4.Pin_0, R5.Pin_0, R6.Pin_0, C1.+
  N4: J3.pin4, J6.pin2, J7.pin4, IC1.pin8, C1.-
  N5: J5.pin1, IC1.pin1
  N6: J5.pin2, IC1.pin2
  N7: J5.pin3, IC1.pin3
  N8: J5.pin4, IC1.pin4
  N9: J5.pin5, J7.pin2
  N10: J5.pin6, J7.pin1
  N11: IC1.pin13, J8.pin2, LED3.cathode
  N12: IC1.pin14, J8.pin3, LED2.cathode
  N13: IC1.pin15, J8.pin4, LED1.cathode
  N14: IC1.pin16, J8.pin5, LED4.cathode
  N15: R3.Pin_1, LED3.anode
  N16: LED1.anode, R4.Pin_1
  N17: LED2.anode, R5.Pin_1
  N18: LED4.anode, R6.Pin_1

notes:
  GND
  3V3
  SDA
  CLK
  RX
  TX
  GPIO1
  GPIO2
  T-SIM7000 / 7070G-S3
  XIAO - UART - SM
  SM - T-SIM7000 / 7070G
  GPIO3
  GPIO4
  A
  B
  C
  D
  ULN2003
