# Fritzing sketch SIM7000-Vision-Shield-Relais (saved by Fritzing 1.0.6)
circuit board: 6cm x 3.55cm
breadboards: 1

parts:
  J3 = female pin header, 16 pins [form="♀ (female)"]
  J1 = female pin header, 16 pins [form="♀ (female)"]  # not connected
  R1 = Resistor [tolerance=±5% resistance=1k power=0.25W package=THT]
  R2 = Resistor [tolerance=±5% resistance=1k power=0.25W package=THT]
  Q1 = NPN-Transistor [part_number=BC337 package="TO92 [THT]"]
  Q2 = NPN-Transistor [part_number=BC337 package="TO92 [THT]"]
  J8 = screw terminal, 3 pins
  LED1 = LED - 3mm [color="Red (633nm)" current=0.030A package="3 mm [THT]"]
  LED2 = LED - 3mm [color="Red (633nm)" current=0.030A package="3 mm [THT]"]
  D3 = Rectifier Diode [part_number=1N4001 package="300 mil [THT]"]
  D4 = Rectifier Diode [part_number=1N4001 package="300 mil [THT]"]
  J9 = screw terminal, 3 pins
  K2 = RELAY [package=relay-g5v]
  K1 = RELAY [package=relay-g5v]
  J19 = male pin header, 4 pins [form="♂ (male)"]
  J20 = female pin header, 7 pins [form="♀ (female)"]
  J21 = female pin header, 7 pins [form="♀ (female)"]

nets:
  N1: J3.pin3, D3.cathode, D4.cathode, K2.2, K1.2, J19.pin3, J21.pin5
  N2: J3.pin4, J21.pin6
  N3: J3.pin5, J19.pin1, J20.pin2
  N4: J3.pin6, J19.pin2, J20.pin3
  N5: J3.pin15, Q1.C, Q2.C, J19.pin4
  N6: R1.Pin_0, R1.Pin_1, LED2.cathode, J20.pin6
  N7: R2.Pin_0, LED1.cathode
  N8: R2.Pin_1, J20.pin7
  N9: Q1.E, D3.anode, K1.9
  N10: Q1.B, LED2.anode
  N11: Q2.E, D4.anode, K2.9
  N12: Q2.B, LED1.anode
  N13: J8.pin1, K1.1
  N14: J8.pin2, K1.6
  N15: J8.pin3, K1.10
  N16: J9.pin1, K2.1
  N17: J9.pin2, K2.6
  N18: J9.pin3, K2.10

notes:
  GND
  3V3
  NC
  NO
  C
  T-SIM7000/7070G-S3
  VISION - I2C
  SDA
  VISION T-SIM7000/7070G
  D9
  D10
  TX
  SCL
  D8
  D3
  D2
  D1
  D0
  D7/TX
  RX
