# Fritzing sketch SIM7080-DRV8825-Shield VOID (saved by Fritzing 1.0.6)
circuit board: 6cm x 3.55cm
breadboards: 1

parts:
  J3 = female pin header, 16 pins [form="♀ (female)"]
  J5 = female pin header, 7 pins [form="♀ (female)"]
  J6 = female pin header, 7 pins [form="♀ (female)"]
  J1 = female pin header, 16 pins [form="♀ (female)"]
  J7 = male pin header, 4 pins [form="♂ (male)"]
  R3 = Resistor [tolerance=±5% resistance=470 power=0.25W package=THT]
  LED1 = LED - 3mm [color="Yellow (595nm)" current=0.030A package="3 mm [THT]"]
  LED2 = LED - 3mm [color="Yellow (595nm)" current=0.030A package="3 mm [THT]"]
  LED3 = LED - 3mm [color="Yellow (595nm)" current=0.030A package="3 mm [THT]"]
  LED4 = LED - 3mm [color="Yellow (595nm)" current=0.030A package="3 mm [THT]"]
  R4 = Resistor [tolerance=±5% resistance=470 power=0.25W package=THT]
  R5 = Resistor [tolerance=±5% resistance=470 power=0.25W package=THT]
  R6 = Resistor [tolerance=±5% resistance=470 power=0.25W package=THT]
  C1 = Electrolytic Capacitor [capacitance=10µF voltage=35V package="100 mil [THT, electrolytic]"]
  J12 = female pin header, 8 pins [form="♀ (female)"]
  J11 = female pin header, 8 pins [form="♀ (female)"]
  J13 = Screw terminal - 2 pins [package=THT]
  J8 = male pin header, 5 pins [form="♂ (male)"]

nets:
  N1: J3.pin1, J3.pin2, J6.pin3, J7.pin3, J12.pin3, J12.pin4
  N2: J3.pin15, J7.pin4, C1.-, J11.pin1, J11.pin7, J13.pin1
  N3: J5.pin1, J12.pin1
  N4: J5.pin2, J12.pin2
  N5: J5.pin5, J7.pin2
  N6: J5.pin6, J7.pin1
  N7: J5.pin7, J1.pin5
  N8: J6.pin7, J1.pin4
  N9: R3.Pin_0, LED2.anode, R4.Pin_0, R5.Pin_0, R5.Pin_1, R6.Pin_0, C1.+, J11.pin8, J13.pin2
  N10: R3.Pin_1, LED3.anode
  N11: LED1.cathode, J11.pin5, J8.pin4
  N12: LED1.anode, R4.Pin_1
  N13: LED2.cathode, J11.pin4, J8.pin3
  N14: LED3.cathode, J11.pin3, J8.pin2
  N15: LED4.cathode, J11.pin6, J8.pin5
  N16: LED4.anode, R6.Pin_1

notes:
  GND
  3V3
  SDA
  CLK
  RX
  TX
  GPIO1
  GPIO2
  T-SIM7080G-S3
  XIAO-UART SM/DRV
  SM/DRV T-SIM7080G
  GPIO3
  GPIO4
  DRV8825
  DC5
  B2
  B1
  A1
  A2
  NC
  VMOT
  RESET
  SLEEP
  STEP
  EN
  M1
  M2
  DIR
  M0
  9-12 V
  +  -
