# Fritzing sketch SIM7080-ULN2003-Shield (saved by Fritzing 1.0.6)
circuit board: 6cm x 3.55cm
breadboards: 1

parts:
  J3 = female pin header, 16 pins [form="♀ (female)"]
  J5 = female pin header, 7 pins [form="♀ (female)"]
  J6 = female pin header, 7 pins [form="♀ (female)"]
  J1 = female pin header, 16 pins [form="♀ (female)"]
  J7 = male pin header, 4 pins [form="♂ (male)"]
  IC1 = IC, DIP package, 16 pins [chip_label=ULN2003]
  R3 = Resistor [tolerance=±5% resistance=470 power=0.25W package=THT]
  LED1 = LED - 3mm [color="Yellow (595nm)" current=0.030A package="3 mm [THT]"]
  LED2 = LED - 3mm [color="Yellow (595nm)" current=0.030A package="3 mm [THT]"]
  LED3 = LED - 3mm [color="Yellow (595nm)" current=0.030A package="3 mm [THT]"]
  LED4 = LED - 3mm [color="Yellow (595nm)" current=0.030A package="3 mm [THT]"]
  R4 = Resistor [tolerance=±5% resistance=470 power=0.25W package=THT]
  R5 = Resistor [tolerance=±5% resistance=470 power=0.25W package=THT]
  R6 = Resistor [tolerance=±5% resistance=470 power=0.25W package=THT]
  C1 = Electrolytic Capacitor [capacitance=10µF voltage=35V package="100 mil [THT, electrolytic]"]
  J9 = male pin header, 2 pins [form="♂ (male)"]
  J10 = male pin header, 2 pins [form="♂ (male)"]
  J8 = male pin header, 5 pins [form="♂ (male)"]

nets:
  N1: J3.pin1, J3.pin2, J6.pin3, J7.pin3, J9.pin1
  N2: J3.pin15, J6.pin2, J7.pin4
  N3: J5.pin1, IC1.pin1
  N4: J5.pin2, IC1.pin2
  N5: J5.pin3, IC1.pin3
  N6: J5.pin4, IC1.pin4
  N7: J5.pin5, J7.pin2
  N8: J5.pin6, J7.pin1
  N9: J5.pin7, J1.pin5
  N10: J6.pin7, J1.pin4
  N11: J1.pin16, R3.Pin_0, LED2.anode, R4.Pin_0, R5.Pin_0, R5.Pin_1, R6.Pin_0, C1.+, J9.pin2, J10.pin1, J10.pin2, J8.pin1
  N12: IC1.pin8, C1.-
  N13: IC1.pin13, LED3.cathode, J8.pin2
  N14: IC1.pin14, LED2.cathode, J8.pin3
  N15: IC1.pin15, LED1.cathode, J8.pin4
  N16: IC1.pin16, LED4.cathode, J8.pin5
  N17: R3.Pin_1, LED3.anode
  N18: LED1.anode, R4.Pin_1
  N19: LED4.anode, R6.Pin_1

notes:
  GND
  3V3
  SDA
  CLK
  RX
  TX
  GPIO1
  GPIO2
  T-SIM7080G-S3
  XIAO - UART - SM
  Rev. A
  SM - T-SIM7080G
  GPIO3
  GPIO4
  A
  B
  C
  D
  ULN2003
  DC5
  5V
