# Fritzing sketch SIM7080-Vision-Shield-TB6612FNG (saved by Fritzing 1.0.6)
circuit board: 6cm x 3.55cm
breadboards: 1

parts:
  J3 = female pin header, 16 pins [form="♀ (female)"]
  J5 = female pin header, 7 pins [form="♀ (female)"]
  J6 = female pin header, 7 pins [form="♀ (female)"]
  J1 = female pin header, 16 pins [form="♀ (female)"]
  R3 = Resistor [tolerance=±5% resistance=470 power=0.25W package=THT]
  LED1 = LED - 3mm [color="Yellow (595nm)" current=0.030A package="3 mm [THT]"]
  LED3 = LED - 3mm [color="Yellow (595nm)" current=0.030A package="3 mm [THT]"]
  LED4 = LED - 3mm [color="Yellow (595nm)" current=0.030A package="3 mm [THT]"]
  R4 = Resistor [tolerance=±5% resistance=470 power=0.25W package=THT]
  R5 = Resistor [tolerance=±5% resistance=470 power=0.25W package=THT]
  R6 = Resistor [tolerance=±5% resistance=470 power=0.25W package=THT]
  C1 = Electrolytic Capacitor [capacitance=10µF voltage=35V package="100 mil [THT, electrolytic]"]
  J12 = female pin header, 8 pins [form="♀ (female)"]
  J11 = female pin header, 8 pins [form="♀ (female)"]
  LED2 = LED - 3mm [color="Yellow (595nm)" current=0.030A package="3 mm [THT]"]
  J17 = Screw terminal - 2 pins [package=THT]
  J8 = male pin header, 5 pins [form="♂ (male)"]
  J16 = male pin header, 3 pins [form="♂ (male)"]
  R7 = Resistor [tolerance=±5% power=0.25W resistance=10k package=THT]
  J18 = male pin header, 4 pins [form="♂ (male)"]
  J13 = male pin header, 2 pins [form="♂ (male)"]
  J14 = male pin header, 2 pins [form="♂ (male)"]

nets:
  N1: J3.pin1, J3.pin2, J5.pin5, J11.pin2, J16.pin1, R7.Pin_1, J18.pin3
  N2: J3.pin15, J5.pin6, C1.-, J12.pin8, J11.pin3, J11.pin8, J17.pin1, J18.pin4
  N3: J5.pin3, J12.pin1
  N4: J5.pin4, J12.pin2
  N5: J6.pin2, J1.pin6, J18.pin1
  N6: J6.pin3, J1.pin7, J18.pin2
  N7: J6.pin4, J12.pin3
  N8: J6.pin5, J12.pin5
  N9: J6.pin6, J12.pin6
  N10: J6.pin7, J12.pin7
  N11: J1.pin16, J16.pin3
  N12: R3.Pin_0, R4.Pin_0, R5.Pin_0, R6.Pin_0, C1.+, J11.pin1, J17.pin2, J16.pin2
  N13: R3.Pin_1, LED3.anode
  N14: LED1.cathode, J11.pin6, J8.pin4, J14.pin1
  N15: LED1.anode, R6.Pin_1
  N16: LED3.cathode, J11.pin4, J8.pin2, J13.pin1
  N17: LED4.cathode, J11.pin7, J8.pin5, J14.pin2
  N18: LED4.anode, R4.Pin_1
  N19: R5.Pin_1, LED2.anode
  N20: J12.pin4, R7.Pin_0
  N21: J11.pin5, LED2.cathode, J8.pin3, J13.pin2

notes:
  GND
  3V3
  SDA
  RX
  D7/TX
  D0
  D1
  SCL
  T-SIM7080G-S3
  SM/DRV-VISION-I2C
  TX
  SM/DRV-VISION-I2C-7080G
  D2
  D3
  TB6612FNG
  B2
  A2
  A1
  VCC
  B1
  STBY
  AIN1
  AIN2
  BIN2
  BIN1
  PWMA
  PWMB
  DC5
  D10
  D9
  CH1
  CH2
  + EXT
  +  -
  + -
  D8
