# Fritzing sketch SIM7080-XIAO-Shield-2 (saved by Fritzing 0.9.5d)
circuit board: 6cm x 3.55cm
breadboards: 1

parts:
  J3 = female pin header, 16 pins [form="♀ (female)"]
  J5 = female pin header, 7 pins [form="♀ (female)"]
  J6 = female pin header, 7 pins [form="♀ (female)"]
  J1 = female pin header, 16 pins [form="♀ (female)"]
  R1 = Resistor [tolerance=±5% resistance=1k package=THT]
  R2 = Resistor [tolerance=±5% resistance=1k package=THT]
  K1 = Relay [part_number="JRC-21F 4100 6Pins 3V" package=THT]
  Q1 = NPN-Transistor [part_number=BC337 package="TO92 [THT]"]
  K2 = Relay [part_number="JRC-21F 4100 6Pins 3V" package=THT]
  Q2 = NPN-Transistor [part_number=BC337 package="TO92 [THT]"]
  J8 = screw terminal, 3 pins
  J7 = male pin header, 4 pins [form="♂ (male)"]
  LED1 = LED - 3mm [color="Red (633nm)" package="3 mm [THT]"]
  LED2 = LED - 3mm [color="Red (633nm)" package="3 mm [THT]"]
  D3 = Rectifier Diode [part_number=1N4001 package="300 mil [THT]"]
  D4 = Rectifier Diode [part_number=1N4001 package="300 mil [THT]"]
  J9 = screw terminal, 3 pins

nets:
  N1: J3.pin1, J3.pin2, J6.pin3, K1.COIL1, K2.COIL1, J7.pin3, D3.cathode, D4.cathode
  N2: J3.pin15, J6.pin2, Q1.C, Q2.C, J7.pin4
  N3: J5.pin1, R1.Pin_1
  N4: J5.pin2, R2.Pin_1
  N5: J5.pin5, J7.pin2
  N6: J5.pin6, J7.pin1
  N7: J5.pin7, J1.pin5
  N8: J6.pin7, J1.pin4
  N9: R1.Pin_0, Q1.B
  N10: R2.Pin_0, Q2.B
  N11: K1.A, J8.pin1
  N12: K1.C1, K1.C2, J8.pin2
  N13: K1.COIL2, LED2.cathode, D3.anode
  N14: K1.B, J8.pin3
  N15: Q1.E, LED2.anode
  N16: K2.A, J9.pin1
  N17: K2.C1, K2.C2, J9.pin2
  N18: K2.COIL2, LED1.cathode, D4.anode
  N19: K2.B, J9.pin3
  N20: Q2.E, LED1.anode

notes:
  GND
  3V3
  SDA
  CLK
  TX
  GPIO1
  GPIO2
  NC
  C
  NO
  T-SIM7080G-S3
  XIAO - UART
