# Fritzing sketch SIM7080-XIAO-Shield (saved by Fritzing 0.9.5d)
circuit board: 6cm x 3.55cm
breadboards: 1

parts:
  J2 = female pin header, 7 pins [form="♀ (female)"]
  J4 = female pin header, 7 pins [form="♀ (female)"]
  J3 = female pin header, 16 pins [form="♀ (female)"]
  J5 = female pin header, 7 pins [form="♀ (female)"]
  J6 = female pin header, 7 pins [form="♀ (female)"]
  J7 = male pin header, 4 pins [form="♂ (male)"]
  J1 = female pin header, 16 pins [form="♀ (female)"]

nets:
  N1: J2.pin1, J5.pin1
  N2: J2.pin2, J5.pin2
  N3: J2.pin3, J5.pin3
  N4: J2.pin4, J5.pin4
  N5: J2.pin5, J5.pin5, J7.pin2
  N6: J2.pin6, J5.pin6, J7.pin1
  N7: J2.pin7, J5.pin7, J1.pin5
  N8: J4.pin1, J6.pin1
  N9: J4.pin2, J6.pin2, J7.pin4, J1.pin2
  N10: J4.pin3, J3.pin2, J6.pin3, J7.pin3
  N11: J4.pin4, J6.pin4
  N12: J4.pin5, J6.pin5
  N13: J4.pin6, J6.pin6
  N14: J4.pin7, J6.pin7, J1.pin4
