# Fritzing sketch Dual-Vision-Shield-Relais (saved by Fritzing 1.0.6)
circuit board: 6cm x 3.55cm
breadboards: 1

parts:
  J3 = female pin header, 16 pins [form="♀ (female)"]  # not connected
  J1 = female pin header, 16 pins [form="♀ (female)"]
  R1 = Resistor [tolerance=±5% resistance=1k power=0.25W package=THT]
  R2 = Resistor [tolerance=±5% resistance=1k power=0.25W package=THT]
  Q1 = NPN-Transistor [part_number=BC337 package="TO92 [THT]"]
  Q2 = NPN-Transistor [part_number=BC337 package="TO92 [THT]"]
  J8 = screw terminal, 3 pins
  LED1 = LED - 3mm [color="Red (633nm)" current=0.030A package="3 mm [THT]"]
  LED2 = LED - 3mm [color="Red (633nm)" current=0.030A package="3 mm [THT]"]
  D3 = Rectifier Diode [part_number=1N4001 package="300 mil [THT]"]
  D4 = Rectifier Diode [part_number=1N4001 package="300 mil [THT]"]
  J9 = screw terminal, 3 pins
  K2 = RELAY [package=relay-g5v]
  K1 = RELAY [package=relay-g5v]
  J20 = female pin header, 7 pins [form="♀ (female)"]
  J21 = female pin header, 7 pins [form="♀ (female)"]
  J22 = male pin header, 4 pins [form="♂ (male)"]
  R3 = Resistor [tolerance=±5% power=0.25W resistance=4.7k package=THT]
  R4 = Resistor [tolerance=±5% power=0.25W resistance=4.7k package=THT]  # not connected

nets:
  N1: J1.pin1, D3.cathode, D4.cathode, K2.2, K1.2, J21.pin5, J22.pin3
  N2: J1.pin2, Q1.C, Q2.C, J21.pin6, J22.pin4, R3.Pin_1
  N3: J1.pin3, J20.pin3, J22.pin2
  N4: J1.pin4, J20.pin2, J22.pin1
  N5: J1.pin7, R2.Pin_0
  N6: J1.pin8, R1.Pin_0
  N7: R1.Pin_1, LED2.cathode
  N8: R2.Pin_1, LED1.cathode
  N9: Q1.E, D3.anode, K1.9
  N10: Q1.B, LED2.anode
  N11: Q2.E, D4.anode, K2.9
  N12: Q2.B, LED1.anode
  N13: J8.pin1, K1.1
  N14: J8.pin2, K1.6
  N15: J8.pin3, K1.10
  N16: J9.pin1, K2.1
  N17: J9.pin2, K2.6
  N18: J9.pin3, K2.10

notes:
  GND
  NC
  NO
  C
  RLY-VISION-I2C
  SDA
  SCL
  3V3
  D0
  D1
  D2
  D3
  D4
  D5
  D6
  D7
  T-SIM7xxx-S3
  RLY-VISION-I2
